// Digital circuit main.dig as structural Verilog
module main (
);

  wire AI, alu_1_p2, AO, BI, BO, BUS, carry, clk, EO, reg_a_1_p5, SU, zero;
  wire [1:0] undriven;
  wire [15:0] eeprom_2_d;

  EEPROM eeprom_1 (.A(undriven), .D(eeprom_2_d[0]));  // open: CS, WE, OE
  EEPROM eeprom_2 (.A(undriven), .D(eeprom_2_d[8]));  // open: CS, WE, OE
  Driver driver_1 (.in(eeprom_2_d[0]), .out(BUS));  // open: en
  // REG_A reg_a_1: pin names not known; wires that end beside it: BUS, clk, AI, AO, reg_a_1_p5, BUS
  // ALU alu_1: pin names not known; wires that end beside it: reg_a_1_p5, alu_1_p2, SU, EO, BUS, carry, zero
  // REG_B reg_b_1: pin names not known; wires that end beside it: BUS, clk, BI, BO, alu_1_p2, BUS
  // Pins of 1 and 8 bits meet at eeprom_2_d[7:0]
  // Pins of 1 and 8 bits meet at eeprom_2_d[15:8]
  // Pins of 1 and 16 bits meet at eeprom_2_d
endmodule
